// Logisim project 3b_XOR.circ as structural Verilog: 2 circuits, main circuit main
module main (
);

  MyXOR myxor_1 ();  // open: in_1, in_2, out_3
  MyXOR myxor_2 ();  // open: in_1, in_2, out_3
endmodule

module MyXOR (
  input  in_1,
  input  in_2,
  output out_3
);

  wire and_1_out, and_2_out, not_1_out, not_2_out;

  not not_1 (not_1_out, in_1);
  not not_2 (not_2_out, in_2);
  and and_1 (and_1_out, not_1_out, in_2);
  and and_2 (and_2_out, in_1, not_2_out);
  or or_1 (out_3, and_1_out, and_2_out);
endmodule
