// Logisim project Adders.circ as structural Verilog: 6 circuits, main circuit FA0
module FA0 (
  input  a,
  input  b,
  output s,
  output c
);

  wire nor_1_out;

  nor nor_1 (nor_1_out, a, b);
  and and_1 (c, a, b);
  nor nor_2 (s, nor_1_out, c);

  // Notes on the sheet:
  //   14 transistors
  //   FA0
  //   Saffron Liu
  //   2.75
  //   1.75
endmodule

module FA1 (
  input  a,
  input  b,
  output s,
  output c
);

  wire nand_1_out;

  nand nand_1 (nand_1_out, a, b);
  or or_1 (c, a, b);
  nand nand_2 (s, nand_1_out, c);

  // Notes on the sheet:
  //   14 transistors
  //   FA1
  //   Saffron Liu
  //   2.75
  //   1.75
endmodule

module FAopt1 (
  input  A,
  input  B,
  input  Cin,
  output S,
  output Cout
);

  wire nand_1_out, nand_2_out, nor_1_out, nor_2_out, nor_3_out, not_1_out, not_2_out;

  nor nor_1 (nor_1_out, A, B);
  nand nand_1 (nand_1_out, A, B);
  not not_1 (not_1_out, nand_1_out);
  nor nor_2 (nor_2_out, nor_1_out, not_1_out);
  nand nand_2 (nand_2_out, nor_2_out, Cin);
  nor nor_3 (nor_3_out, nor_2_out, Cin);
  not not_2 (not_2_out, nand_2_out);
  nand nand_3 (Cout, nand_1_out, nand_2_out);
  nor nor_4 (S, nor_3_out, not_2_out);

  // Notes on the sheet:
  //   32 transistors
  //   FAopt1
  //   Saffron Liu
  //   If Cin < 2.75: 5.5
  //   If Cin < 2.75: 4.75
  //   If Cin > 2.75: Cin + 2
  //   If Cin > 2.75: Cin + 2.75
endmodule

module FAopt2 (
  input  A,
  input  B,
  input  Cin,
  output S,
  output Cout
);

  wire and_1_out, nand_1_out, nand_2_out, nand_3_out, nor_1_out, nor_2_out, nor_3_out, not_1_out;

  nor nor_1 (nor_1_out, A, B);
  nand nand_1 (nand_1_out, A, B);
  nand nand_2 (nand_2_out, A, Cin);
  nand nand_3 (nand_3_out, B, Cin);
  not not_1 (not_1_out, nand_1_out);
  nand nand_4 (Cout, nand_1_out, nand_2_out, nand_3_out);
  nor nor_2 (nor_2_out, nor_1_out, not_1_out);
  nor nor_3 (nor_3_out, nor_2_out, Cin);
  and and_1 (and_1_out, nor_2_out, Cin);
  nor nor_4 (S, nor_3_out, and_1_out);

  // Notes on the sheet:
  //   42 transistors
  //   Cin + 2.25
  //   FAopt2
  //   Saffron Liu
  //   If Cin < 2.75: 5.5
  //   If Cin > 2.75: Cin + 2.75
endmodule

module Ripple4Bit (
  input  [3:0] A,
  input  [3:0] B,
  output [3:0] S,
  output Cout
);

  wire fa0_1_c, faopt1_2_cout, faopt2_1_cout;

  FAopt1 faopt1_1 (.A(A[3]), .B(B[3]), .Cin(faopt1_2_cout), .Cout(Cout), .S(S[3]));
  FAopt1 faopt1_2 (.A(A[2]), .B(B[2]), .Cin(faopt2_1_cout), .Cout(faopt1_2_cout), .S(S[2]));
  FAopt2 faopt2_1 (.A(A[1]), .B(B[1]), .Cin(fa0_1_c), .Cout(faopt2_1_cout), .S(S[1]));
  FA0 fa0_1 (.a(A[0]), .b(B[0]), .s(S[0]), .c(fa0_1_c));

  // Notes on the sheet:
  //   8
  //   6
  //   8.75
  //   4
  //   6.75
  //   1.75
  //   2.75
  //   5.5
  //   120 transistors
  //   4-bit Ripple Carry Adder
  //   Saffron Liu
endmodule

module Ripple8Bit (
  input  [7:0] A,
  input  [7:0] B,
  output [7:0] S,
  output Cout
);

  wire fa0_1_c, faopt1_2_cout, faopt1_3_cout, faopt1_4_cout, faopt1_5_cout, faopt1_6_cout, faopt2_1_cout;

  FAopt1 faopt1_1 (.A(A[7]), .B(B[7]), .Cin(faopt1_2_cout), .Cout(Cout), .S(S[7]));
  FAopt1 faopt1_2 (.A(A[6]), .B(B[6]), .Cin(faopt1_3_cout), .Cout(faopt1_2_cout), .S(S[6]));
  FAopt1 faopt1_3 (.A(A[5]), .B(B[5]), .Cin(faopt1_4_cout), .Cout(faopt1_3_cout), .S(S[5]));
  FAopt1 faopt1_4 (.A(A[4]), .B(B[4]), .Cin(faopt1_5_cout), .Cout(faopt1_4_cout), .S(S[4]));
  FAopt1 faopt1_5 (.A(A[3]), .B(B[3]), .Cin(faopt1_6_cout), .Cout(faopt1_5_cout), .S(S[3]));
  FAopt1 faopt1_6 (.A(A[2]), .B(B[2]), .Cin(faopt2_1_cout), .Cout(faopt1_6_cout), .S(S[2]));
  FAopt2 faopt2_1 (.A(A[1]), .B(B[1]), .Cin(fa0_1_c), .Cout(faopt2_1_cout), .S(S[1]));
  FA0 fa0_1 (.a(A[0]), .b(B[0]), .s(S[0]), .c(fa0_1_c));

  // Notes on the sheet:
  //   16
  //   14
  //   16.75
  //   12
  //   14.75
  //   10
  //   12.75
  //   8
  //   10.75
  //   6
  //   8.75
  //   4
  //   6.75
  //   1.75
  //   5.5
  //   2.75
  //   248 transistors
  //   8-bit Ripple Carry Adder
  //   Saffron Liu
endmodule
